// Logisim project sonHali.circ as structural Verilog
module main (
  input  in_1,
  input  R,
  input  in_3,
  input  Clck,
  output [3:0] out_5,
  output [3:0] out_6,
  output [15:0] out_7,
  output out_8,
  output [15:0] out_9
);

  wire deneme_1_memread, deneme_1_memwrite, deneme_1_mux1, mux3, mux4, mux5, Mux6, pCLOCK, PcRead, PcWrite,
       push, spliti_nstruction_1_cin, we;
  wire [1:0] deneme_1_aluc, mux2;
  wire [3:0] deneme_1_wregister, spliti_nstruction_1__9_12;
  wire [15:0] adder_1_out, alu_1_output, multiplexer_1_out, multiplexer_2_out, multiplexer_3_out,
       multiplexer_4_out, multiplexer_5_out, Mux4Output, Mux5Output, n16_bit_adder_1_s, n16_bit_adder_2_s,
       n16_bit_register_1_out, n16_bit_register_2_out, ram_1_data, rgisterfile_1_output1,
       rgisterfile_1_output2, spliti_nstruction_1__0_3, spliti_nstruction_1__0_8, spliti_nstruction_1__0_12;

  // Probe on Mux5Output
  Multiplexer #(.width(16), .enable("false")) multiplexer_1 (
    .in0(n16_bit_adder_1_s), .in1(n16_bit_adder_2_s), .out(multiplexer_1_out), .sel(push));
  _16_bit_Register u_16_bit_register_1 (
    .\input (Mux5Output), .L_S_S_0_L_1(in_1), .R(R), .E(1'b1), .Clck(PcWrite), .out(n16_bit_register_1_out));
  _16_bit_adder u_16_bit_adder_1 (
    .\cİ (1'b0), .a(n16_bit_register_2_out), .b(16'h1), .s(n16_bit_adder_1_s));  // open: cO
  _16_bit_adder u_16_bit_adder_2 (
    .\cİ (1'b0), .a(n16_bit_register_2_out), .b({16{1'b1}}), .s(n16_bit_adder_2_s));  // open: cO
  _16_bit_Register u_16_bit_register_2 (
    .\input (multiplexer_1_out), .L_S_S_0_L_1(in_3), .R(R), .E(1'b1), .Clck(pCLOCK),
    .out(n16_bit_register_2_out));
  // Probe on n16_bit_register_2_out
  // Probe on n16_bit_register_1_out
  _16_bit_adder u_16_bit_adder_3 (.\cİ (1'b0), .a(n16_bit_register_1_out), .b(16'h1), .s(out_9));  // open: cO
  ROM #(.addrWidth(16), .dataWidth(16)) rom_1 (.addr(n16_bit_register_1_out), .data(out_7));  // open: sel
  \Splitİnstruction  \spliti̇nstruction_1  (
    .in_1(out_7), ._0_12(spliti_nstruction_1__0_12), ._9_12(spliti_nstruction_1__9_12),
    ._0_3(spliti_nstruction_1__0_3), .cin(spliti_nstruction_1_cin), ._0_8(spliti_nstruction_1__0_8));
  // Probe on Mux4Output
  // Probe on spliti_nstruction_1__0_12
  RgisterFile rgisterfile_1 (
    .Rr1(out_6), .Rr2(out_5), .output1(rgisterfile_1_output1), .R(R), .W_R_E(we),
    .output2(rgisterfile_1_output2), .\input (Mux4Output), .Wre(deneme_1_wregister), .Clck(Clck));
  // Probe on out_9
  Adder #(.width(16)) adder_1 (.a(spliti_nstruction_1__0_12), .b(out_9), .out(adder_1_out));  // open: cin, cout
  // Probe on rgisterfile_1_output1
  // Probe on spliti_nstruction_1__0_3
  // Probe on rgisterfile_1_output2
  Multiplexer #(.width(16), .enable("false")) multiplexer_2 (
    .in0(spliti_nstruction_1__0_8), .in1(n16_bit_register_2_out), .out(multiplexer_2_out), .sel(Mux6));
  // Probe on spliti_nstruction_1_cin
  // Probe on adder_1_out
  Deneme deneme_1 (
    .Insruction(out_7), .rd1(out_6), .rd2(out_5), .Clck(Clck), .Mux2(mux2), .Mux3(mux3), .Mux4(mux4),
    .Mux5(mux5), .MemRead(deneme_1_memread), .AluC(deneme_1_aluc), .we(we), .wregister(deneme_1_wregister),
    .memWrite(deneme_1_memwrite), .PcWrite(PcWrite), .PcRead(PcRead), .Mux6(Mux6), .PUSH(push),
    .pCLOKC(pCLOCK), .Mux1(deneme_1_mux1));  // open: out_12, out_18, out_14
  Multiplexer #(.width(16), .enable("false")) multiplexer_3 (
    .in0(rgisterfile_1_output2), .in1(spliti_nstruction_1__0_3), .out(multiplexer_3_out), .sel(deneme_1_mux1));
  ALU alu_1 (
    .\cİn (1'b0), .a(rgisterfile_1_output1), .b(multiplexer_3_out), .select(deneme_1_aluc), .cOut(out_8),
    .\output (alu_1_output));
  // Probe on deneme_1_aluc
  // Probe on alu_1_output
  Multiplexer #(.select(2), .width(16), .enable("false")) multiplexer_4 (
    .in0(alu_1_output), .in1(multiplexer_2_out), .in3(adder_1_out), .out(multiplexer_4_out), .sel(mux2));  // open: in2
  // Probe on mux2
  // Probe on multiplexer_4_out
  RAM #(.addrWidth(16), .dataWidth(16), .bus("separate")) ram_1 (
    .addr(multiplexer_4_out), .din(rgisterfile_1_output1), .data(ram_1_data), .str(deneme_1_memwrite),
    .sel(1'b1), .clk(Clck), .ld(deneme_1_memread), .clr(1'b0));
  // Probe on multiplexer_4_out
  // Probe on ram_1_data
  Multiplexer #(.width(16), .enable("false")) multiplexer_5 (
    .in0(ram_1_data), .in1(multiplexer_4_out), .out(multiplexer_5_out), .sel(mux3));
  Multiplexer #(.width(16), .enable("false")) multiplexer_6 (
    .in0(multiplexer_5_out), .in1(out_9), .out(Mux4Output), .sel(mux4));
  // Probe on multiplexer_5_out
  // Probe on Mux5Output
  Multiplexer #(.width(16), .enable("false")) multiplexer_7 (
    .in0(multiplexer_5_out), .in1(out_9), .out(Mux5Output), .sel(mux5));

  // Notes on the sheet:
  //   StackPointer
  //   contents of rom_1 (hex, n*v repeats v):
  //   0 201 402 603 804 a05 c06 e07 1008 1209 140a 160b 180c 1a0d 1c0e 1e0f 2002 0 0 9400 6600 cfd0 f1b1
  //   aacd b927 5000
  //   Mux1
  //   Mux2
  //   Mux3
  //   Mux 4
  //   Mux5
endmodule

module D_Latch (
  input  D,
  input  C,
  input  R,
  output Q
);

  wire and_1_out, and_2_out, nor_1_out, not_1_out;

  not not_1 (not_1_out, D);
  and and_1 (and_1_out, D, C);
  and and_2 (and_2_out, C, not_1_out);
  nor nor_1 (nor_1_out, and_1_out, Q);
  nor nor_2 (Q, nor_1_out, R, and_2_out);
endmodule

module _16_bit_Register (
  input  [15:0] \input ,
  input  L_S_S_0_L_1,
  input  R,
  input  E,
  input  Clck,
  output [15:0] out
);

  wire multiplexer_1_out, multiplexer_2_out, multiplexer_3_out, multiplexer_4_out, multiplexer_5_out,
       multiplexer_6_out, multiplexer_7_out, multiplexer_8_out, multiplexer_9_out, multiplexer_10_out,
       multiplexer_11_out, multiplexer_12_out, multiplexer_13_out, multiplexer_14_out, multiplexer_15_out,
       multiplexer_16_out;

  Multiplexer #(.enable("false")) multiplexer_1 (
    .in0(\input [0]), .in1(out[0]), .out(multiplexer_1_out), .sel(L_S_S_0_L_1));
  D_Flip_Flop_part i0 (.clk(Clck), .D(multiplexer_1_out), .Q(out[0]), .en(E), .reset(R));  // open: Qn, preset
  Multiplexer #(.enable("false")) multiplexer_2 (
    .in0(\input [1]), .in1(out[1]), .out(multiplexer_2_out), .sel(L_S_S_0_L_1));
  D_Flip_Flop_part i1 (.clk(Clck), .D(multiplexer_2_out), .Q(out[1]), .en(E), .reset(R));  // open: Qn, preset
  Multiplexer #(.enable("false")) multiplexer_3 (
    .in0(\input [2]), .in1(out[2]), .out(multiplexer_3_out), .sel(L_S_S_0_L_1));
  D_Flip_Flop_part i2 (.clk(Clck), .D(multiplexer_3_out), .Q(out[2]), .en(E), .reset(R));  // open: Qn, preset
  Multiplexer #(.enable("false")) multiplexer_4 (
    .in0(\input [3]), .in1(out[3]), .out(multiplexer_4_out), .sel(L_S_S_0_L_1));
  D_Flip_Flop_part i3 (.clk(Clck), .D(multiplexer_4_out), .Q(out[3]), .en(E), .reset(R));  // open: Qn, preset
  Multiplexer #(.enable("false")) multiplexer_5 (
    .in0(\input [4]), .in1(out[4]), .out(multiplexer_5_out), .sel(L_S_S_0_L_1));
  D_Flip_Flop_part i4 (.clk(Clck), .D(multiplexer_5_out), .Q(out[4]), .en(E), .reset(R));  // open: Qn, preset
  Multiplexer #(.enable("false")) multiplexer_6 (
    .in0(\input [5]), .in1(out[5]), .out(multiplexer_6_out), .sel(L_S_S_0_L_1));
  D_Flip_Flop_part i5 (.clk(Clck), .D(multiplexer_6_out), .Q(out[5]), .en(E), .reset(R));  // open: Qn, preset
  Multiplexer #(.enable("false")) multiplexer_7 (
    .in0(\input [6]), .in1(out[6]), .out(multiplexer_7_out), .sel(L_S_S_0_L_1));
  D_Flip_Flop_part i6 (.clk(Clck), .D(multiplexer_7_out), .Q(out[6]), .en(E), .reset(R));  // open: Qn, preset
  Multiplexer #(.enable("false")) multiplexer_8 (
    .in0(\input [7]), .in1(out[7]), .out(multiplexer_8_out), .sel(L_S_S_0_L_1));
  D_Flip_Flop_part i7 (.clk(Clck), .D(multiplexer_8_out), .Q(out[7]), .en(E), .reset(R));  // open: Qn, preset
  Multiplexer #(.enable("false")) multiplexer_9 (
    .in0(\input [8]), .in1(out[8]), .out(multiplexer_9_out), .sel(L_S_S_0_L_1));
  D_Flip_Flop_part i8 (.clk(Clck), .D(multiplexer_9_out), .Q(out[8]), .en(E), .reset(R));  // open: Qn, preset
  Multiplexer #(.enable("false")) multiplexer_10 (
    .in0(\input [9]), .in1(out[9]), .out(multiplexer_10_out), .sel(L_S_S_0_L_1));
  D_Flip_Flop_part i9 (.clk(Clck), .D(multiplexer_10_out), .Q(out[9]), .en(E), .reset(R));  // open: Qn, preset
  Multiplexer #(.enable("false")) multiplexer_11 (
    .in0(\input [10]), .in1(out[10]), .out(multiplexer_11_out), .sel(L_S_S_0_L_1));
  D_Flip_Flop_part i10 (.clk(Clck), .D(multiplexer_11_out), .Q(out[10]), .en(E), .reset(R));  // open: Qn, preset
  Multiplexer #(.enable("false")) multiplexer_12 (
    .in0(\input [11]), .in1(out[11]), .out(multiplexer_12_out), .sel(L_S_S_0_L_1));
  D_Flip_Flop_part i10_2 (.clk(Clck), .D(multiplexer_12_out), .Q(out[11]), .en(E), .reset(R));  // open: Qn, preset
  Multiplexer #(.enable("false")) multiplexer_13 (
    .in0(\input [12]), .in1(out[12]), .out(multiplexer_13_out), .sel(L_S_S_0_L_1));
  D_Flip_Flop_part i10_3 (.clk(Clck), .D(multiplexer_13_out), .Q(out[12]), .en(E), .reset(R));  // open: Qn, preset
  Multiplexer #(.enable("false")) multiplexer_14 (
    .in0(\input [13]), .in1(out[13]), .out(multiplexer_14_out), .sel(L_S_S_0_L_1));
  D_Flip_Flop_part i13 (.clk(Clck), .D(multiplexer_14_out), .Q(out[13]), .en(E), .reset(R));  // open: Qn, preset
  Multiplexer #(.enable("false")) multiplexer_15 (
    .in0(\input [14]), .in1(out[14]), .out(multiplexer_15_out), .sel(L_S_S_0_L_1));
  D_Flip_Flop_part i14 (.clk(Clck), .D(multiplexer_15_out), .Q(out[14]), .en(E), .reset(R));  // open: Qn, preset
  Multiplexer #(.enable("false")) multiplexer_16 (
    .in0(\input [15]), .in1(out[15]), .out(multiplexer_16_out), .sel(L_S_S_0_L_1));
  D_Flip_Flop_part i15 (.clk(Clck), .D(multiplexer_16_out), .Q(out[15]), .en(E), .reset(R));  // open: Qn, preset
endmodule

module D_Flip_Flop (
  input  R,
  input  D,
  input  Clock,
  output Q
);

  wire d_latch_1_q, not_1_out;

  not not_1 (not_1_out, Clock);
  D_Latch d_latch_1 (.D(D), .R(R), .C(not_1_out), .Q(d_latch_1_q));
  D_Latch d_latch_2 (.D(d_latch_1_q), .R(R), .C(Clock), .Q(Q));
endmodule

module RgisterFile (
  input  [3:0] Rr1,
  input  [3:0] Rr2,
  input  R,
  input  W_R_E,
  input  [15:0] \input ,
  input  [3:0] Wre,
  input  Clck,
  output [15:0] output1,
  output [15:0] output2
);

  wire decoder_1_out0, decoder_1_out1, decoder_1_out2, decoder_1_out3, decoder_1_out4, decoder_1_out5,
       decoder_1_out6, decoder_1_out7, decoder_1_out8, decoder_1_out9, decoder_1_out10, decoder_1_out11,
       decoder_1_out12, decoder_1_out13, decoder_1_out14, decoder_1_out15, decoder_2_out0, decoder_2_out1,
       decoder_2_out2, decoder_2_out3, decoder_2_out4, decoder_2_out5, decoder_2_out6, decoder_2_out7,
       decoder_2_out8, decoder_2_out9, decoder_2_out10, decoder_2_out11, decoder_2_out12, decoder_2_out13,
       decoder_2_out14, decoder_2_out15, decoder_3_out0, decoder_3_out1, decoder_3_out2, decoder_3_out3,
       decoder_3_out4, decoder_3_out5, decoder_3_out6, decoder_3_out7, decoder_3_out8, decoder_3_out9,
       decoder_3_out10, decoder_3_out11, decoder_3_out12, decoder_3_out13, decoder_3_out14, decoder_3_out15,
       not_1_out;
  wire [15:0] i2_out, i15_out, n16_bit_register_1_out, n16_bit_register_2_out, r1_out, r3_out, r4_out,
       r6_out, r7_out, r8_out, r9_out, r10_out, r11_out, r12_out, r13_out, r14_out;

  Decoder #(.select(4)) decoder_1 (
    .out0(decoder_1_out0), .out1(decoder_1_out1), .out2(decoder_1_out2), .out3(decoder_1_out3),
    .out4(decoder_1_out4), .out5(decoder_1_out5), .out6(decoder_1_out6), .out7(decoder_1_out7),
    .out8(decoder_1_out8), .out9(decoder_1_out9), .out10(decoder_1_out10), .out11(decoder_1_out11),
    .out12(decoder_1_out12), .out13(decoder_1_out13), .out14(decoder_1_out14), .out15(decoder_1_out15),
    .sel(Rr1));  // open: en
  Decoder #(.select(4)) decoder_2 (
    .out0(decoder_2_out0), .out1(decoder_2_out1), .out2(decoder_2_out2), .out3(decoder_2_out3),
    .out4(decoder_2_out4), .out5(decoder_2_out5), .out6(decoder_2_out6), .out7(decoder_2_out7),
    .out8(decoder_2_out8), .out9(decoder_2_out9), .out10(decoder_2_out10), .out11(decoder_2_out11),
    .out12(decoder_2_out12), .out13(decoder_2_out13), .out14(decoder_2_out14), .out15(decoder_2_out15),
    .sel(Rr2));  // open: en
  Decoder #(.select(4), .enable("false")) decoder_3 (
    .out0(decoder_3_out0), .out1(decoder_3_out1), .out2(decoder_3_out2), .out3(decoder_3_out3),
    .out4(decoder_3_out4), .out5(decoder_3_out5), .out6(decoder_3_out6), .out7(decoder_3_out7),
    .out8(decoder_3_out8), .out9(decoder_3_out9), .out10(decoder_3_out10), .out11(decoder_3_out11),
    .out12(decoder_3_out12), .out13(decoder_3_out13), .out14(decoder_3_out14), .out15(decoder_3_out15),
    .sel(Wre));
  // Probe on r12_out
  not not_1 (not_1_out, W_R_E);
  // Probe on r3_out
  _16_bit_Register u_16_bit_register_1 (
    .\input (\input ), .L_S_S_0_L_1(not_1_out), .R(R), .E(decoder_3_out0), .Clck(Clck),
    .out(n16_bit_register_1_out));
  _16_bit_Register r1 (
    .\input (\input ), .L_S_S_0_L_1(not_1_out), .R(R), .E(decoder_3_out1), .Clck(Clck), .out(r1_out));
  _16_bit_Register i2 (
    .\input (\input ), .L_S_S_0_L_1(not_1_out), .R(R), .E(decoder_3_out2), .Clck(Clck), .out(i2_out));
  _16_bit_Register r3 (
    .\input (\input ), .L_S_S_0_L_1(not_1_out), .R(R), .E(decoder_3_out3), .Clck(Clck), .out(r3_out));
  _16_bit_Register r6 (
    .\input (\input ), .L_S_S_0_L_1(not_1_out), .R(R), .E(decoder_3_out6), .Clck(Clck), .out(r6_out));
  _16_bit_Register r7 (
    .\input (\input ), .L_S_S_0_L_1(not_1_out), .R(R), .E(decoder_3_out7), .Clck(Clck), .out(r7_out));
  _16_bit_Register r8 (
    .\input (\input ), .L_S_S_0_L_1(not_1_out), .R(R), .E(decoder_3_out8), .Clck(Clck), .out(r8_out));
  _16_bit_Register r10 (
    .\input (\input ), .L_S_S_0_L_1(not_1_out), .R(R), .E(decoder_3_out10), .Clck(Clck), .out(r10_out));
  _16_bit_Register r11 (
    .\input (\input ), .L_S_S_0_L_1(not_1_out), .R(R), .E(decoder_3_out11), .Clck(Clck), .out(r11_out));
  _16_bit_Register r12 (
    .\input (\input ), .L_S_S_0_L_1(not_1_out), .R(R), .E(decoder_3_out12), .Clck(Clck), .out(r12_out));
  _16_bit_Register r13 (
    .\input (\input ), .L_S_S_0_L_1(not_1_out), .R(R), .E(decoder_3_out13), .Clck(Clck), .out(r13_out));
  _16_bit_Register r14 (
    .\input (\input ), .L_S_S_0_L_1(not_1_out), .R(R), .E(decoder_3_out14), .Clck(Clck), .out(r14_out));
  _16_bit_Register i15 (
    .\input (\input ), .L_S_S_0_L_1(not_1_out), .R(R), .E(decoder_3_out15), .Clck(Clck), .out(i15_out));
  // Probe on n16_bit_register_1_out
  _16_bit_Register r4 (
    .\input (\input ), .L_S_S_0_L_1(not_1_out), .R(R), .E(decoder_3_out4), .Clck(Clck), .out(r4_out));
  _16_bit_Register u_16_bit_register_2 (
    .\input (\input ), .L_S_S_0_L_1(not_1_out), .R(R), .E(decoder_3_out5), .Clck(Clck),
    .out(n16_bit_register_2_out));
  _16_bit_Register r9 (
    .\input (\input ), .L_S_S_0_L_1(not_1_out), .R(R), .E(decoder_3_out9), .Clck(Clck), .out(r9_out));
  assign output2 = decoder_2_out0 ? n16_bit_register_1_out : 16'bz;  // Controlled_Buffer controlled_buffer_1
  assign output2 = decoder_2_out1 ? r1_out : 16'bz;  // Controlled_Buffer controlled_buffer_2
  assign output2 = decoder_2_out2 ? i2_out : 16'bz;  // Controlled_Buffer controlled_buffer_3
  assign output2 = decoder_2_out3 ? r3_out : 16'bz;  // Controlled_Buffer controlled_buffer_4
  assign output2 = decoder_2_out4 ? r4_out : 16'bz;  // Controlled_Buffer controlled_buffer_5
  assign output2 = decoder_2_out5 ? n16_bit_register_2_out : 16'bz;  // Controlled_Buffer controlled_buffer_6
  assign output2 = decoder_2_out6 ? r6_out : 16'bz;  // Controlled_Buffer controlled_buffer_7
  assign output2 = decoder_2_out7 ? r7_out : 16'bz;  // Controlled_Buffer controlled_buffer_8
  assign output2 = decoder_2_out8 ? r8_out : 16'bz;  // Controlled_Buffer controlled_buffer_9
  assign output2 = decoder_2_out9 ? r9_out : 16'bz;  // Controlled_Buffer controlled_buffer_10
  assign output2 = decoder_2_out10 ? r10_out : 16'bz;  // Controlled_Buffer controlled_buffer_11
  assign output2 = decoder_2_out11 ? r11_out : 16'bz;  // Controlled_Buffer controlled_buffer_12
  assign output2 = decoder_2_out12 ? r12_out : 16'bz;  // Controlled_Buffer controlled_buffer_13
  assign output2 = decoder_2_out13 ? r13_out : 16'bz;  // Controlled_Buffer controlled_buffer_14
  assign output2 = decoder_2_out14 ? r14_out : 16'bz;  // Controlled_Buffer controlled_buffer_15
  assign output2 = decoder_2_out15 ? i15_out : 16'bz;  // Controlled_Buffer controlled_buffer_16
  assign output1 = decoder_1_out0 ? n16_bit_register_1_out : 16'bz;  // Controlled_Buffer controlled_buffer_17
  assign output1 = decoder_1_out1 ? r1_out : 16'bz;  // Controlled_Buffer controlled_buffer_18
  assign output1 = decoder_1_out2 ? i2_out : 16'bz;  // Controlled_Buffer controlled_buffer_19
  assign output1 = decoder_1_out3 ? r3_out : 16'bz;  // Controlled_Buffer controlled_buffer_20
  assign output1 = decoder_1_out4 ? r4_out : 16'bz;  // Controlled_Buffer controlled_buffer_21
  assign output1 = decoder_1_out5 ? n16_bit_register_2_out : 16'bz;  // Controlled_Buffer controlled_buffer_22
  assign output1 = decoder_1_out6 ? r6_out : 16'bz;  // Controlled_Buffer controlled_buffer_23
  assign output1 = decoder_1_out7 ? r7_out : 16'bz;  // Controlled_Buffer controlled_buffer_24
  assign output1 = decoder_1_out8 ? r8_out : 16'bz;  // Controlled_Buffer controlled_buffer_25
  assign output1 = decoder_1_out9 ? r9_out : 16'bz;  // Controlled_Buffer controlled_buffer_26
  assign output1 = decoder_1_out10 ? r10_out : 16'bz;  // Controlled_Buffer controlled_buffer_27
  assign output1 = decoder_1_out11 ? r11_out : 16'bz;  // Controlled_Buffer controlled_buffer_28
  assign output1 = decoder_1_out12 ? r12_out : 16'bz;  // Controlled_Buffer controlled_buffer_29
  assign output1 = decoder_1_out13 ? r13_out : 16'bz;  // Controlled_Buffer controlled_buffer_30
  assign output1 = decoder_1_out14 ? r14_out : 16'bz;  // Controlled_Buffer controlled_buffer_31
  assign output1 = decoder_1_out15 ? i15_out : 16'bz;  // Controlled_Buffer controlled_buffer_32
endmodule

module ControlUnit (
  input  [15:0] Insruction,
  output [3:0] rd1,
  output [3:0] rd2,
  output [3:0] wr
);

  wire not_1_out, not_2_out, not_3_out, not_4_out, not_5_out, not_6_out, not_7_out, not_8_out, not_9_out,
       not_10_out;

  // AND_Gate LD has open pins: in0=not_1_out, in1=not_2_out, in2=not_3_out, out=open
  // AND_Gate JMP has open pins: in0=not_4_out, in1=not_5_out, in2=Insruction[13], out=open
  // AND_Gate St has open pins: in0=not_6_out, in1=Insruction[14], in2=not_7_out, out=open
  // AND_Gate Pop has open pins: in0=Insruction[13], in1=Insruction[14], in2=not_8_out, out=open
  // AND_Gate Push has open pins: in0=not_9_out, in1=not_10_out, in2=Insruction[15], out=open
  Multiplexer #(.width(4), .enable("false")) multiplexer_1 ();  // open: in0, in1, out, sel
  not not_1 (not_1_out, Insruction[13]);
  not not_2 (not_2_out, Insruction[14]);
  not not_3 (not_3_out, Insruction[15]);
  not not_4 (not_4_out, Insruction[15]);
  not not_5 (not_5_out, Insruction[14]);
  not not_6 (not_6_out, Insruction[13]);
  not not_7 (not_7_out, Insruction[15]);
  not not_8 (not_8_out, Insruction[15]);
  not not_9 (not_9_out, Insruction[13]);
  not not_10 (not_10_out, Insruction[14]);
  Bit_Extender #(.in_width(1), .out_width(4), .\type ("sign")) bit_extender_1 ();  // open: in, out
endmodule

module FSM (
  input  b,
  input  [2:0] opcode,
  input  clr,
  input  Clk,
  output [3:0] xgerecek,
  output [2:0] out_6,
  output [2:0] out_7
);

  wire and_1_out, and_2_out, and_3_out, comparator_1_eq, comparator_2_eq, comparator_3_eq, not_1_out,
       not_2_out, not_3_out, not_4_out, not_5_out, not_6_out, not_7_out, not_8_out, not_9_out, not_10_out,
       not_11_out, not_12_out, not_13_out, not_14_out, not_15_out, not_16_out, not_17_out, not_18_out,
       not_19_out, not_20_out, not_21_out, not_22_out, not_23_out, not_24_out, not_25_out, not_26_out,
       not_27_out, not_28_out, not_29_out, not_30_out, not_31_out, not_32_out, not_33_out, not_34_out,
       or_1_out, or_2_out, or_3_out, state3_out, state4_out, x1_2_out, x1_out, x2_out, x3_out, x4_out,
       x5_out, x6_out, x7_out, x8_out, x9_out, x10_out, x11_out, x12_out, x13_out, x14_out;
  wire [3:0] controlled_buffer_6_out;

  and x1 (x1_out, not_5_out, not_6_out, not_1_out, not_7_out);
  not not_1 (not_1_out, b);
  not not_2 (not_2_out, out_7[2]);
  and and_1 (and_1_out, not_2_out, out_7[0], out_7[1], not_31_out, not_32_out, opcode[0]);
  and and_2 (and_2_out, not_3_out, not_4_out, out_7[2]);
  or or_1 (or_1_out, and_1_out, and_2_out);
  Register #(.width(3)) register_1 (.D(out_6), .en(1'b1), .Q(out_7), .clk(Clk));  // open: clr
  not not_3 (not_3_out, out_7[0]);
  not not_4 (not_4_out, out_7[1]);
  or or_2 (or_2_out, or_1_out, x1_out, and_3_out);
  not not_5 (not_5_out, out_7[0]);
  not not_6 (not_6_out, out_7[1]);
  not not_7 (not_7_out, out_7[2]);
  not not_8 (not_8_out, out_7[1]);
  not not_9 (not_9_out, out_7[2]);
  not not_10 (not_10_out, out_7[0]);
  not not_11 (not_11_out, out_7[2]);
  not not_12 (not_12_out, out_7[2]);
  not not_13 (not_13_out, out_7[0]);
  not not_14 (not_14_out, out_7[2]);
  not not_15 (not_15_out, out_7[2]);
  not not_16 (not_16_out, out_7[0]);
  not not_17 (not_17_out, out_7[2]);
  not not_18 (not_18_out, out_7[2]);
  not not_19 (not_19_out, out_7[0]);
  not not_20 (not_20_out, out_7[2]);
  not not_21 (not_21_out, out_7[2]);
  not not_22 (not_22_out, out_7[0]);
  not not_23 (not_23_out, out_7[2]);
  not not_24 (not_24_out, out_7[0]);
  not not_25 (not_25_out, out_7[2]);
  not not_26 (not_26_out, out_7[0]);
  not not_27 (not_27_out, out_7[2]);
  not not_28 (not_28_out, out_7[0]);
  not not_29 (not_29_out, out_7[2]);
  not not_30 (not_30_out, opcode[0]);
  not not_31 (not_31_out, opcode[1]);
  not not_32 (not_32_out, opcode[2]);
  assign out_6 = x1_2_out ? 3'b001 : 3'bz;  // Controlled_Buffer controlled_buffer_1
  assign out_6 = x2_out ? 3'b010 : 3'bz;  // Controlled_Buffer controlled_buffer_2
  assign out_6 = state3_out ? 3'b011 : 3'bz;  // Controlled_Buffer controlled_buffer_3
  assign out_6 = state4_out ? 3'b100 : 3'bz;  // Controlled_Buffer controlled_buffer_4
  assign out_6 = or_2_out ? 3'b000 : 3'bz;  // Controlled_Buffer controlled_buffer_5
  and x1_2 (x1_2_out, b, not_5_out, not_6_out, not_7_out);
  and x2 (x2_out, b, out_7[0], not_8_out, not_9_out);
  and x3 (x3_out, not_10_out, out_7[1], not_11_out, not_30_out, not_31_out, not_32_out);
  and x4 (x4_out, out_7[0], out_7[1], not_12_out, not_30_out, not_31_out, not_32_out);
  and x5 (x5_out, not_13_out, out_7[1], not_14_out, not_30_out, opcode[1], not_32_out);
  and x6 (x6_out, out_7[0], out_7[1], not_15_out, not_30_out, opcode[1], not_32_out);
  and x7 (x7_out, not_16_out, out_7[1], not_17_out, opcode[0], opcode[1], not_32_out);
  and x8 (x8_out, out_7[0], out_7[1], not_18_out, not_32_out, opcode[0], opcode[1]);
  and x9 (x9_out, not_19_out, out_7[1], not_20_out, not_30_out, not_31_out, opcode[2]);
  and x10 (x10_out, out_7[0], out_7[1], not_21_out, not_30_out, not_31_out, opcode[2]);
  and x11 (x11_out, not_22_out, out_7[1], not_23_out, opcode[0], not_31_out, not_32_out);
  and x12 (x12_out, not_24_out, out_7[1], not_25_out, opcode[0], not_31_out, opcode[2]);
  and x13 (x13_out, not_26_out, out_7[1], not_27_out, not_30_out, opcode[1], opcode[2]);
  and x14 (x14_out, not_28_out, out_7[1], not_29_out, opcode[0], opcode[1], opcode[2]);
  or state3 (state3_out, x14_out, x13_out, x12_out, x11_out, x9_out, x7_out, x5_out, x3_out);
  assign controlled_buffer_6_out = x1_out ? 4'b0000 : 4'bz;  // Controlled_Buffer controlled_buffer_6
  or state4 (state4_out, x10_out, x8_out, x6_out, x4_out);
  not not_33 (not_33_out, x1_2_out);
  not not_34 (not_34_out, or_1_out);
  assign controlled_buffer_6_out = x1_2_out ? 4'b0001 : 4'bz;  // Controlled_Buffer controlled_buffer_7
  assign controlled_buffer_6_out = x2_out ? 4'b0010 : 4'bz;  // Controlled_Buffer controlled_buffer_8
  assign controlled_buffer_6_out = x3_out ? 4'b0011 : 4'bz;  // Controlled_Buffer controlled_buffer_9
  assign controlled_buffer_6_out = x4_out ? 4'b0100 : 4'bz;  // Controlled_Buffer controlled_buffer_10
  assign controlled_buffer_6_out = x5_out ? 4'b0101 : 4'bz;  // Controlled_Buffer controlled_buffer_11
  assign controlled_buffer_6_out = x7_out ? 4'b0111 : 4'bz;  // Controlled_Buffer controlled_buffer_12
  assign controlled_buffer_6_out = x8_out ? 4'b1000 : 4'bz;  // Controlled_Buffer controlled_buffer_13
  assign controlled_buffer_6_out = x9_out ? 4'b1001 : 4'bz;  // Controlled_Buffer controlled_buffer_14
  assign controlled_buffer_6_out = x10_out ? 4'b1010 : 4'bz;  // Controlled_Buffer controlled_buffer_15
  assign controlled_buffer_6_out = x11_out ? 4'b1011 : 4'bz;  // Controlled_Buffer controlled_buffer_16
  assign controlled_buffer_6_out = x12_out ? 4'b1100 : 4'bz;  // Controlled_Buffer controlled_buffer_17
  assign controlled_buffer_6_out = x13_out ? 4'b1101 : 4'bz;  // Controlled_Buffer controlled_buffer_18
  assign controlled_buffer_6_out = x14_out ? 4'b1110 : 4'bz;  // Controlled_Buffer controlled_buffer_19
  assign controlled_buffer_6_out = x6_out ? 4'b0110 : 4'bz;  // Controlled_Buffer controlled_buffer_20
  and and_3 (and_3_out, or_3_out, not_33_out, not_34_out);
  Register #(.width(4)) register_2 (.D(controlled_buffer_6_out), .Q(xgerecek), .clk(Clk));  // open: en, clr
  Comparator #(.width(4), .mode("unsigned")) comparator_1 (
    .a(xgerecek), .b(4'b1100), .eq(comparator_1_eq));  // open: gt, lt
  Comparator #(.width(4), .mode("unsigned")) comparator_2 (
    .a(4'b1101), .b(xgerecek), .eq(comparator_2_eq));  // open: gt, lt
  Comparator #(.width(4), .mode("unsigned")) comparator_3 (
    .a(4'b1110), .b(xgerecek), .eq(comparator_3_eq));  // open: gt, lt
  or or_3 (or_3_out, comparator_1_eq, comparator_2_eq, comparator_3_eq);
endmodule

module _3_bitRegister (
  input  [2:0] nstate,
  input  L_S,
  input  Clc,
  output [2:0] Cstate
);

  wire multiplexer_1_out, multiplexer_2_out, multiplexer_3_out;

  Multiplexer #(.enable("false")) multiplexer_1 (.in0(nstate[0]), .in1(Cstate[0]), .out(multiplexer_1_out), .sel(L_S));
  D_Flip_Flop i0 (.D(multiplexer_1_out), .Clock(Clc), .Q(Cstate[0]));  // open: R
  Multiplexer #(.enable("false")) multiplexer_2 (.in0(nstate[1]), .in1(Cstate[1]), .out(multiplexer_2_out), .sel(L_S));
  D_Flip_Flop i1 (.D(multiplexer_2_out), .Clock(Clc), .Q(Cstate[1]));  // open: R
  Multiplexer #(.enable("false")) multiplexer_3 (.in0(nstate[2]), .in1(Cstate[2]), .out(multiplexer_3_out), .sel(L_S));
  D_Flip_Flop i2 (.D(multiplexer_3_out), .Clock(Clc), .Q(Cstate[2]));  // open: R
endmodule

module ControlUnit2 (
  input  [15:0] Insruction,
  input  in_2,
  input  in_3,
  output [3:0] rd1,
  output [3:0] rd2,
  output [2:0] out_6,
  output [3:0] wr,
  output [3:0] out_8,
  output [2:0] out_9
);

  wire Alu_out, decoder_1_out0, decoder_1_out1, decoder_1_out2, LD_out, not_1_out, not_2_out, not_3_out,
       not_4_out, not_5_out, not_6_out, not_7_out, not_8_out, not_9_out, or_1_out, or_2_out, or_3_out,
       or_4_out, pop_out, push_out, St_out;
  wire [3:0] controlled_buffer_3_out, multiplexer_1_out;

  assign rd1 = Alu_out ? multiplexer_1_out : 4'bz;  // Controlled_Buffer controlled_buffer_1
  not not_1 (not_1_out, Insruction[4]);
  assign rd2 = not_1_out ? controlled_buffer_3_out : 4'bz;  // Controlled_Buffer controlled_buffer_2
  Multiplexer #(.width(4), .enable("false")) multiplexer_1 (
    .in0(Insruction[8:5]), .in1(Insruction[12:9]), .out(multiplexer_1_out), .sel(or_1_out));
  or or_1 (or_1_out, push_out, pop_out, St_out);
  assign controlled_buffer_3_out = Alu_out ? Insruction[3:0] : 4'bz;  // Controlled_Buffer controlled_buffer_3
  assign wr = or_2_out ? Insruction[12:9] : 4'bz;  // Controlled_Buffer controlled_buffer_4
  or or_2 (or_2_out, Alu_out, LD_out);
  not not_2 (not_2_out, Insruction[13]);
  not not_3 (not_3_out, Insruction[14]);
  and LD (LD_out, not_2_out, not_3_out, not_4_out);
  not not_4 (not_4_out, Insruction[15]);
  not not_5 (not_5_out, Insruction[13]);
  and St (St_out, not_5_out, Insruction[14], not_6_out);
  not not_6 (not_6_out, Insruction[15]);
  and pop (pop_out, Insruction[13], Insruction[14], not_7_out);
  not not_7 (not_7_out, Insruction[15]);
  not not_8 (not_8_out, Insruction[13]);
  not not_9 (not_9_out, Insruction[14]);
  and push (push_out, not_8_out, not_9_out, Insruction[15]);
  or or_3 (or_3_out, Insruction[13], Insruction[14]);
  and Alu (Alu_out, or_3_out, Insruction[15]);
  FSM fsm_1 (
    .b(or_4_out), .opcode(Insruction[15:13]), .clr(in_2), .Clk(in_3), .xgerecek(out_8), .out_6(out_9));  // open: out_7
  or or_4 (or_4_out, decoder_1_out0, decoder_1_out1);
  Decoder #(.select(4), .enable("false")) decoder_1 (
    .out0(decoder_1_out0), .out1(decoder_1_out1), .out2(decoder_1_out2), .sel(out_8));  // open: out3, out4, out5, out6, out7, out8, out9, out10, out11, out12, out13, out14, out15

  assign out_6 = Insruction[15:13];
endmodule

module Deneme (
  input  [15:0] Insruction,
  input  Clck,
  output Mux1,
  output [1:0] Mux2,
  output Mux3,
  output Mux4,
  output Mux5,
  output MemRead,
  output [1:0] AluC,
  output we,
  output [3:0] rd1,
  output [3:0] out_12,
  output [3:0] rd2,
  output [2:0] out_14,
  output [3:0] wregister,
  output memWrite,
  output PcWrite,
  output [2:0] out_18,
  output PcRead,
  output Mux6,
  output PUSH,
  output pCLOKC
);

  wire Alu_out, and_1_out, and_2_out, decoder_1_out1, decoder_1_out2, decoder_1_out3, decoder_1_out4,
       decoder_1_out5, decoder_1_out6, decoder_1_out7, decoder_1_out8, decoder_1_out9, decoder_1_out12,
       decoder_1_out13, decoder_1_out14, LD_out, not_1_out, not_2_out, not_3_out, not_4_out, not_5_out,
       not_6_out, not_7_out, not_8_out, not_9_out, not_10_out, not_12_out, not_13_out, not_14_out,
       not_15_out, not_16_out, or_1_out, or_3_out, or_4_out, or_5_out, or_6_out, pop_out, push_out, rd1flag,
       St_out;
  wire [1:0] counter_1_q;
  wire [3:0] controlled_buffer_3_out, multiplexer_1_out;

  assign rd1 = or_1_out ? multiplexer_1_out : 4'bz;  // Controlled_Buffer controlled_buffer_1
  or or_1 (or_1_out, rd1flag, Alu_out);
  not not_1 (not_1_out, Insruction[4]);
  assign rd2 = not_1_out ? controlled_buffer_3_out : 4'bz;  // Controlled_Buffer controlled_buffer_2
  Multiplexer #(.width(4), .enable("false")) multiplexer_1 (
    .in0(Insruction[8:5]), .in1(Insruction[12:9]), .out(multiplexer_1_out), .sel(rd1flag));
  or or_2 (rd1flag, push_out, St_out);
  assign controlled_buffer_3_out = Alu_out ? Insruction[3:0] : 4'bz;  // Controlled_Buffer controlled_buffer_3
  assign wregister = or_3_out ? Insruction[12:9] : 4'bz;  // Controlled_Buffer controlled_buffer_4
  or or_3 (or_3_out, Alu_out, pop_out, LD_out);
  and LD (LD_out, not_2_out, not_3_out, not_4_out);
  and St (St_out, not_5_out, Insruction[14], not_6_out);
  and pop (pop_out, Insruction[13], Insruction[14], not_7_out);
  and u_push (push_out, not_8_out, not_9_out, Insruction[15]);
  and Alu (Alu_out, or_4_out, Insruction[15]);
  not not_2 (not_2_out, Insruction[13]);
  not not_3 (not_3_out, Insruction[14]);
  not not_4 (not_4_out, Insruction[15]);
  not not_5 (not_5_out, Insruction[13]);
  not not_6 (not_6_out, Insruction[15]);
  not not_7 (not_7_out, Insruction[15]);
  not not_8 (not_8_out, Insruction[13]);
  not not_9 (not_9_out, Insruction[14]);
  or or_4 (or_4_out, Insruction[13], Insruction[14]);
  FSM fsm_1 (
    .b(or_5_out), .opcode(Insruction[15:13]), .Clk(Clck), .xgerecek(out_12), .out_6(out_18));  // open: clr, out_7
  or or_5 (or_5_out, decoder_1_out1, PcWrite, decoder_1_out2);
  Decoder #(.select(4), .enable("false")) decoder_1 (
    .out0(PcWrite), .out1(decoder_1_out1), .out2(decoder_1_out2), .out3(decoder_1_out3),
    .out4(decoder_1_out4), .out5(decoder_1_out5), .out6(decoder_1_out6), .out7(decoder_1_out7),
    .out8(decoder_1_out8), .out9(decoder_1_out9), .out10(PUSH), .out11(Mux2[1]), .out12(decoder_1_out12),
    .out13(decoder_1_out13), .out14(decoder_1_out14), .sel(out_12));  // open: out15
  or or_6 (or_6_out, decoder_1_out8, PUSH);
  and and_1 (and_1_out, or_6_out, Clck);
  or or_7 (Mux2[0], decoder_1_out3, decoder_1_out4, decoder_1_out5, decoder_1_out6, decoder_1_out7, decoder_1_out8, decoder_1_out9, PUSH, Mux2[1]);
  and and_2 (and_2_out, PUSH, not_10_out);
  not not_10 (not_10_out, pCLOKC);
  Counter_part #(.width(2), .max('h3)) counter_1 (
    .Q(counter_1_q), .clk(and_1_out), .clr(PcWrite));  // open: load, D, count, carry
  or or_8 (Mux3, Mux2[1], decoder_1_out12, decoder_1_out13, decoder_1_out14);
  not not_11 (Mux5, Mux2[1]);
  or or_9 (MemRead, decoder_1_out3, decoder_1_out8, decoder_1_out4);
  not not_12 (not_12_out, decoder_1_out13);
  not not_13 (not_13_out, decoder_1_out14);
  not not_14 (not_14_out, decoder_1_out14);
  not not_15 (not_15_out, decoder_1_out12);
  or or_10 (memWrite, decoder_1_out6, and_2_out);
  or or_11 (Mux6, decoder_1_out8, decoder_1_out7, PUSH, PUSH);
  // Probe on counter_1_q
  and and_3 (AluC[1], decoder_1_out12, not_12_out, not_13_out);
  and and_4 (AluC[0], not_14_out, decoder_1_out13, not_15_out);
  or or_12 (we, decoder_1_out4, decoder_1_out12, counter_1_q[0], decoder_1_out13, decoder_1_out14);
  not not_16 (not_16_out, counter_1_q[0]);
  and and_5 (pCLOKC, counter_1_q[1], not_16_out);

  assign Mux1 = Insruction[4];
  assign Mux4 = 1'b0;
  assign out_14 = Insruction[15:13];
  assign PcRead = 1'b1;

  // Notes on the sheet:
  //   fetch1
  //   fetch2
  //   Ld1
  //   Ld2
  //   st1
  //   St2
  //   pop1
  //   pop2
  //   push1
  //   push2
  //   jmp
  //   add
  //   and
  //   or
endmodule

module FAdder (
  input  a,
  input  b,
  input  \cİ ,
  output cO,
  output s
);

  wire and_1_out, and_2_out, and_3_out, xor_1_out;

  and and_1 (and_1_out, a, b);
  and and_2 (and_2_out, a, \cİ );
  and and_3 (and_3_out, b, \cİ );
  xor xor_1 (xor_1_out, a, b);
  xor xor_2 (s, xor_1_out, \cİ );
  or or_1 (cO, and_1_out, and_2_out, and_3_out);
endmodule

module _16_bit_adder (
  input  \cİ ,
  input  [15:0] a,
  input  [15:0] b,
  output [15:0] s,
  output cO
);

  wire fadder_1_co, fadder_2_co, fadder_3_co, fadder_4_co, fadder_5_co, fadder_6_co, fadder_7_co,
       fadder_8_co, fadder_9_co, fadder_10_co, i0_co, i1_co, i2_co, i3_co, i4_co;

  FAdder i0 (.a(a[0]), .b(b[0]), .\cİ (\cİ ), .cO(i0_co), .s(s[0]));
  FAdder i1 (.a(a[1]), .b(b[1]), .\cİ (i0_co), .cO(i1_co), .s(s[1]));
  FAdder i2 (.a(a[2]), .b(b[2]), .\cİ (i1_co), .cO(i2_co), .s(s[2]));
  FAdder i3 (.a(a[3]), .b(b[3]), .\cİ (i2_co), .cO(i3_co), .s(s[3]));
  FAdder i4 (.a(a[4]), .b(b[4]), .\cİ (i3_co), .cO(i4_co), .s(s[4]));
  FAdder fadder_1 (.a(a[5]), .b(b[5]), .\cİ (i4_co), .cO(fadder_1_co), .s(s[5]));
  FAdder fadder_2 (.a(a[6]), .b(b[6]), .\cİ (fadder_1_co), .cO(fadder_2_co), .s(s[6]));
  FAdder fadder_3 (.a(a[7]), .b(b[7]), .\cİ (fadder_2_co), .cO(fadder_3_co), .s(s[7]));
  FAdder fadder_4 (.a(a[8]), .b(b[8]), .\cİ (fadder_3_co), .cO(fadder_4_co), .s(s[8]));
  FAdder fadder_5 (.a(a[9]), .b(b[9]), .\cİ (fadder_4_co), .cO(fadder_5_co), .s(s[9]));
  FAdder fadder_6 (.a(a[10]), .b(b[10]), .\cİ (fadder_5_co), .cO(fadder_6_co), .s(s[10]));
  FAdder fadder_7 (.a(a[11]), .b(b[11]), .\cİ (fadder_6_co), .cO(fadder_7_co), .s(s[11]));
  FAdder fadder_8 (.a(a[12]), .b(b[12]), .\cİ (fadder_7_co), .cO(fadder_8_co), .s(s[12]));
  FAdder fadder_9 (.a(a[13]), .b(b[13]), .\cİ (fadder_8_co), .cO(fadder_9_co), .s(s[13]));
  FAdder fadder_10 (.a(a[14]), .b(b[14]), .\cİ (fadder_9_co), .cO(fadder_10_co), .s(s[14]));
  FAdder fadder_11 (.a(a[15]), .b(b[15]), .\cİ (fadder_10_co), .cO(cO), .s(s[15]));
endmodule

// siplit
module \Splitİnstruction  (
  input  [15:0] in_1,
  output [15:0] _0_12,
  output [3:0] _9_12,
  output [15:0] _0_3,
  output cin,
  output [15:0] _0_8
);

  and and_1 (cin, in_1[3], in_1[4]);
  assign _0_3 = {{12{in_1[3]}}, in_1[3:0]};  // Bit_Extender bit_extender_1
  assign _0_12 = {{3{in_1[12]}}, in_1[12:0]};  // Bit_Extender bit_extender_2
  assign _0_8 = {{7{in_1[8]}}, in_1[8:0]};  // Bit_Extender bit_extender_3

  assign _9_12 = in_1[12:9];
endmodule

module ALU (
  input  \cİn ,
  input  [15:0] a,
  input  [15:0] b,
  input  [1:0] select,
  output cOut,
  output [15:0] \output 
);

  wire [15:0] and_1_out, n16_bit_adder_1_s, or_1_out;

  _16_bit_adder u_16_bit_adder_1 (.\cİ (\cİn ), .a(a), .b(b), .s(n16_bit_adder_1_s), .cO(cOut));
  assign and_1_out = a & b;  // AND_Gate and_1, 16 bits wide
  assign or_1_out = a | b;  // OR_Gate or_1, 16 bits wide
  Multiplexer #(.select(2), .width(16), .enable("false")) multiplexer_1 (
    .in0(or_1_out), .in1(and_1_out), .in2(n16_bit_adder_1_s), .out(\output ), .sel(select));  // open: in3

  // Notes on the sheet:
  //   OR 00
  //   AND 01
  //   aDD 10
endmodule

module RegisterFileFinal (
  input  [15:0] \input ,
  input  L_S_S_0_L_1,
  input  R,
  input  E,
  input  Clck,
  output [15:0] out
);

  wire multiplexer_1_out, multiplexer_2_out, multiplexer_3_out, multiplexer_4_out, multiplexer_5_out,
       multiplexer_6_out, multiplexer_7_out, multiplexer_8_out, multiplexer_9_out, multiplexer_10_out,
       multiplexer_11_out, multiplexer_12_out, multiplexer_13_out, multiplexer_14_out, multiplexer_15_out,
       multiplexer_16_out;

  Multiplexer #(.enable("false")) multiplexer_1 (
    .in0(\input [0]), .in1(out[0]), .out(multiplexer_1_out), .sel(L_S_S_0_L_1));
  D_Flip_Flop_part i0 (.clk(Clck), .D(multiplexer_1_out), .Q(out[0]), .en(E), .reset(R));  // open: Qn, preset
  Multiplexer #(.enable("false")) multiplexer_2 (
    .in0(\input [1]), .in1(out[1]), .out(multiplexer_2_out), .sel(L_S_S_0_L_1));
  D_Flip_Flop_part i1 (.clk(Clck), .D(multiplexer_2_out), .Q(out[1]), .en(E), .reset(R));  // open: Qn, preset
  Multiplexer #(.enable("false")) multiplexer_3 (
    .in0(\input [2]), .in1(out[2]), .out(multiplexer_3_out), .sel(L_S_S_0_L_1));
  D_Flip_Flop_part i2 (.clk(Clck), .D(multiplexer_3_out), .Q(out[2]), .en(E), .reset(R));  // open: Qn, preset
  Multiplexer #(.enable("false")) multiplexer_4 (
    .in0(\input [3]), .in1(out[3]), .out(multiplexer_4_out), .sel(L_S_S_0_L_1));
  D_Flip_Flop_part i3 (.clk(Clck), .D(multiplexer_4_out), .Q(out[3]), .en(E), .reset(R));  // open: Qn, preset
  Multiplexer #(.enable("false")) multiplexer_5 (
    .in0(\input [4]), .in1(out[4]), .out(multiplexer_5_out), .sel(L_S_S_0_L_1));
  D_Flip_Flop_part i4 (.clk(Clck), .D(multiplexer_5_out), .Q(out[4]), .en(E), .reset(R));  // open: Qn, preset
  Multiplexer #(.enable("false")) multiplexer_6 (
    .in0(\input [5]), .in1(out[5]), .out(multiplexer_6_out), .sel(L_S_S_0_L_1));
  D_Flip_Flop_part i5 (.clk(Clck), .D(multiplexer_6_out), .Q(out[5]), .en(E), .reset(R));  // open: Qn, preset
  Multiplexer #(.enable("false")) multiplexer_7 (
    .in0(\input [6]), .in1(out[6]), .out(multiplexer_7_out), .sel(L_S_S_0_L_1));
  D_Flip_Flop_part i6 (.clk(Clck), .D(multiplexer_7_out), .Q(out[6]), .en(E), .reset(R));  // open: Qn, preset
  Multiplexer #(.enable("false")) multiplexer_8 (
    .in0(\input [7]), .in1(out[7]), .out(multiplexer_8_out), .sel(L_S_S_0_L_1));
  D_Flip_Flop_part i7 (.clk(Clck), .D(multiplexer_8_out), .Q(out[7]), .en(E), .reset(R));  // open: Qn, preset
  Multiplexer #(.enable("false")) multiplexer_9 (
    .in0(\input [8]), .in1(out[8]), .out(multiplexer_9_out), .sel(L_S_S_0_L_1));
  D_Flip_Flop_part i8 (.clk(Clck), .D(multiplexer_9_out), .Q(out[8]), .en(E), .reset(R));  // open: Qn, preset
  Multiplexer #(.enable("false")) multiplexer_10 (
    .in0(\input [9]), .in1(out[9]), .out(multiplexer_10_out), .sel(L_S_S_0_L_1));
  D_Flip_Flop_part i9 (.clk(Clck), .D(multiplexer_10_out), .Q(out[9]), .en(E), .reset(R));  // open: Qn, preset
  Multiplexer #(.enable("false")) multiplexer_11 (
    .in0(\input [10]), .in1(out[10]), .out(multiplexer_11_out), .sel(L_S_S_0_L_1));
  D_Flip_Flop_part i10 (.clk(Clck), .D(multiplexer_11_out), .Q(out[10]), .en(E), .reset(R));  // open: Qn, preset
  Multiplexer #(.enable("false")) multiplexer_12 (
    .in0(\input [11]), .in1(out[11]), .out(multiplexer_12_out), .sel(L_S_S_0_L_1));
  D_Flip_Flop_part i10_2 (.clk(Clck), .D(multiplexer_12_out), .Q(out[11]), .en(E), .reset(R));  // open: Qn, preset
  Multiplexer #(.enable("false")) multiplexer_13 (
    .in0(\input [12]), .in1(out[12]), .out(multiplexer_13_out), .sel(L_S_S_0_L_1));
  D_Flip_Flop_part i10_3 (.clk(Clck), .D(multiplexer_13_out), .Q(out[12]), .en(E), .reset(R));  // open: Qn, preset
  Multiplexer #(.enable("false")) multiplexer_14 (
    .in0(\input [13]), .in1(out[13]), .out(multiplexer_14_out), .sel(L_S_S_0_L_1));
  D_Flip_Flop_part i10_4 (.clk(Clck), .D(multiplexer_14_out), .Q(out[13]), .en(E), .reset(R));  // open: Qn, preset
  Multiplexer #(.enable("false")) multiplexer_15 (
    .in0(\input [14]), .in1(out[14]), .out(multiplexer_15_out), .sel(L_S_S_0_L_1));
  D_Flip_Flop_part i10_5 (.clk(Clck), .D(multiplexer_15_out), .Q(out[14]), .en(E), .reset(R));  // open: Qn, preset
  Multiplexer #(.enable("false")) multiplexer_16 (
    .in0(\input [15]), .in1(out[15]), .out(multiplexer_16_out), .sel(L_S_S_0_L_1));
  D_Flip_Flop_part i10_6 (.clk(Clck), .D(multiplexer_16_out), .Q(out[15]), .en(E), .reset(R));  // open: Qn, preset
endmodule
